# Fritzing sketch Partybus_D1Mini (saved by Fritzing 0.9.10b)

parts:
  WeMos_D1_Mini1 = WeMos D1 Mini
  Part1 = NeoPixel Stick [part_number=1426]
  MP1584EN_Board1 = MP1584EN Power Regulator Board [part_number=MP1584EN]
  9V = DC Power [voltage=5]

nets:
  3V3: WeMos_D1_Mini1.3V3, Part1.+5V
  N1: WeMos_D1_Mini1.5V, MP1584EN_Board1.OUT_+
  N2: WeMos_D1_Mini1.D8, Part1.DATAIN
  N3: WeMos_D1_Mini1.G, Part1.GND, MP1584EN_Board1.OUT_-
  N4: MP1584EN_Board1.IN_-, 9V.V-
  N5: MP1584EN_Board1.IN_+, 9V.V+

custom parts:
  NeoPixel Stick: Make your own little LED strip arrangement with this stick of NeoPixel LEDs. We crammed 8 of the tiny 5050 (5mm x 5mm) smart RGB LEDs onto a PCB with mounting holes and a chainable design. Use only one microcontroller pin to control as many as you can chain together! Each LED is addressable as the driver chip is inside the LED. Each one has ~18mA constant current drive so the color will be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
  MP1584EN Power Regulator Board: The MP1584EN is a high frequency step-down switching regulator. The input voltage range is 4.5V to 28V. The output voltage is set by the board's potentiometer.
